// Logisim project 8bitcomputer.circ as structural Verilog: 4 circuits, main circuit main
module main (
  input  [7:0] Data,
  input  in_2,
  input  master_reset,
  input  programming_mode,
  input  load,
  input  [7:0] address,
  input  in_7,
  input  in_8,
  input  in_9,
  input  in_10,
  output [7:0] out_11,
  output HLT,
  output AI,
  output AO,
  output BI,
  output BO,
  output SU,
  output ALUO,
  output RO,
  output MAI,
  output RI,
  output II,
  output IO,
  output CE,
  output jump,
  output OI,
  output CO,
  output FI
);

  wire adder_1_cout, and_1_out, and_2_out, bcd_1_a, bcd_1_b, bcd_1_c, bcd_1_d, bcd_1_e, bcd_1_f, bcd_1_g,
       bcd_1_out_11, bcd_2_a, bcd_2_b, bcd_2_c, bcd_2_d, bcd_2_e, bcd_2_f, bcd_2_g, bcd_2_out_11, bcd_3_a,
       bcd_3_b, bcd_3_c, bcd_3_d, bcd_3_e, bcd_3_f, bcd_3_g, bcd_3_out_11, controlled_buffer_9_out,
       controlled_buffer_11_out, main_clock_out, n3_7seg_decodeer_1_y0, n3_7seg_decodeer_1_y1,
       n3_7seg_decodeer_1_y2, n3_7seg_decodeer_1_y3, n3_7seg_decodeer_1_y4, n3_7seg_decodeer_1_y5,
       n3_7seg_decodeer_1_y6, n3_7seg_decodeer_1_y7, n3_7seg_decodeer_1_y8, n3_7seg_decodeer_1_y9, not_1_out,
       not_2_out, not_3_out;
  wire [2:0] counter_1_q;
  wire [3:0] controlled_buffer_14_out;
  wire [5:4] register_6_q;
  wire [7:0] adder_1_out, bit_extender_1_out, controlled_buffer_1_out, controlled_buffer_2_out,
       controlled_buffer_6_out, controlled_buffer_7_out, counter_2_q, not_4_out, Output_register_q,
       ram_1_data, register_1_q, register_2_q, register_3_q, register_4_q, xor_1_out;

  Clock main_clock (.out(main_clock_out));
  and and_1 (and_1_out, main_clock_out, not_1_out);
  not not_1 (not_1_out, HLT);
  assign bit_extender_1_out = {{7{SU}}, SU};  // Bit_Extender bit_extender_1
  assign controlled_buffer_1_out = AI ? out_11 : 8'bz;  // Controlled_Buffer controlled_buffer_1
  Register register_1 (.D(controlled_buffer_1_out), .en(AI), .Q(register_1_q), .clk(and_1_out), .clr(master_reset));
  assign controlled_buffer_2_out = BI ? out_11 : 8'bz;  // Controlled_Buffer controlled_buffer_2
  Register register_2 (.D(controlled_buffer_2_out), .en(BI), .Q(register_2_q), .clk(and_1_out), .clr(master_reset));
  assign xor_1_out = register_2_q ^ bit_extender_1_out;  // XOR_Gate xor_1, 8 bits wide
  assign out_11 = AO ? register_1_q : 8'bz;  // Controlled_Buffer controlled_buffer_3
  assign out_11 = BO ? register_2_q : 8'bz;  // Controlled_Buffer controlled_buffer_4
  Adder adder_1 (.a(register_1_q), .b(xor_1_out), .out(adder_1_out), .cin(SU), .cout(adder_1_cout));
  assign out_11 = ALUO ? adder_1_out : 8'bz;  // Controlled_Buffer controlled_buffer_5
  assign controlled_buffer_6_out = RI ? out_11 : 8'bz;  // Controlled_Buffer controlled_buffer_6
  assign controlled_buffer_7_out = not_3_out ? register_3_q : 8'bz;  // Controlled_Buffer controlled_buffer_7
  assign controlled_buffer_7_out = programming_mode ? address : 8'bz;  // Controlled_Buffer controlled_buffer_8
  Register register_3 (.D(out_11), .en(MAI), .Q(register_3_q), .clk(and_1_out), .clr(master_reset));
  assign controlled_buffer_9_out = not_3_out ? and_1_out : 1'bz;  // Controlled_Buffer controlled_buffer_9
  Register register_4 (.D(out_11), .en(II), .Q(register_4_q), .clk(and_1_out), .clr(master_reset));
  not not_2 (not_2_out, and_1_out);
  assign controlled_buffer_6_out = programming_mode ? Data : 8'bz;  // Controlled_Buffer controlled_buffer_10
  RAM #(.bus("separate")) ram_1 (
    .addr(controlled_buffer_7_out), .din(controlled_buffer_6_out), .data(ram_1_data),
    .str(controlled_buffer_11_out), .sel(1'b1), .clk(controlled_buffer_9_out), .ld(RO), .clr(master_reset));
  assign controlled_buffer_11_out = not_3_out ? RI : 1'bz;  // Controlled_Buffer controlled_buffer_11
  Counter #(.width(3), .max('h7)) counter_1 (
    .Q(counter_1_q), .clk(not_2_out), .clr(master_reset));  // open: load, D, count, carry
  assign out_11 = RO ? ram_1_data : 8'bz;  // Controlled_Buffer controlled_buffer_12
  assign controlled_buffer_11_out = load ? programming_mode : 1'bz;  // Controlled_Buffer controlled_buffer_13
  assign controlled_buffer_14_out = IO ? register_4_q[3:0] : 4'bz;  // Controlled_Buffer controlled_buffer_14
  assign controlled_buffer_9_out = programming_mode ? in_2 : 1'bz;  // Controlled_Buffer controlled_buffer_15
  not not_3 (not_3_out, programming_mode);
  Bit_Extender #(.in_width(4), .out_width(8), .\type ("input")) bit_extender_2 (
    .in(controlled_buffer_14_out), .out(out_11));  // open: extend
  ROM #(.addrWidth(9), .dataWidth(17)) rom_1 (
    .addr({counter_1_q, register_6_q, register_4_q[7:4]}),
    .data({HLT, AI, AO, BI, BO, ALUO, RO, MAI, RI, II, IO, CE, jump, OI, CO, FI, SU}), .sel(1'b1));
  Counter counter_2 (
    .load(jump), .D(out_11), .count(CE), .Q(counter_2_q), .clk(and_1_out), .clr(master_reset));  // open: carry
  assign out_11 = CO ? counter_2_q : 8'bz;  // Controlled_Buffer controlled_buffer_16
  assign not_4_out = ~adder_1_out;  // NOT_Gate not_4, 8 bits wide
  Register Output_register (.D(out_11), .en(OI), .Q(Output_register_q), .clk(and_1_out), .clr(master_reset));
  and and_2 (and_2_out, not_4_out[0], not_4_out[1], not_4_out[2], not_4_out[3], not_4_out[4], not_4_out[5], not_4_out[6], not_4_out[7]);
  Register #(.width(1)) register_5 (.D(and_2_out), .en(FI), .Q(register_6_q[5]), .clk(and_1_out), .clr(master_reset));
  _3_7seg_decodeer u_3_7seg_decodeer_1 (
    .in_1(in_9), .i7(Output_register_q[7]), .in_3(in_10), .i6(Output_register_q[6]),
    .i5(Output_register_q[5]), .i4(Output_register_q[4]), .i3(Output_register_q[3]),
    .i2(Output_register_q[2]), .i1(Output_register_q[1]), .i0(Output_register_q[0]),
    .y9(n3_7seg_decodeer_1_y9), .y8(n3_7seg_decodeer_1_y8), .y7(n3_7seg_decodeer_1_y7),
    .y6(n3_7seg_decodeer_1_y6), .y5(n3_7seg_decodeer_1_y5), .y4(n3_7seg_decodeer_1_y4),
    .y3(n3_7seg_decodeer_1_y3), .y2(n3_7seg_decodeer_1_y2), .y1(n3_7seg_decodeer_1_y1),
    .y0(n3_7seg_decodeer_1_y0));
  Register #(.width(1)) register_6 (
    .D(adder_1_cout), .en(FI), .Q(register_6_q[4]), .clk(and_1_out), .clr(master_reset));
  bcd bcd_1 (
    ._3(in_7), ._2(in_8), ._1(n3_7seg_decodeer_1_y9), .in_4(n3_7seg_decodeer_1_y8), .b(bcd_1_b), .a(bcd_1_a),
    .g(bcd_1_g), .f(bcd_1_f), .c(bcd_1_c), .d(bcd_1_d), .out_11(bcd_1_out_11), .e(bcd_1_e));
  bcd bcd_2 (
    ._3(n3_7seg_decodeer_1_y7), ._2(n3_7seg_decodeer_1_y6), ._1(n3_7seg_decodeer_1_y5),
    .in_4(n3_7seg_decodeer_1_y4), .b(bcd_2_b), .a(bcd_2_a), .g(bcd_2_g), .f(bcd_2_f), .c(bcd_2_c),
    .d(bcd_2_d), .out_11(bcd_2_out_11), .e(bcd_2_e));
  bcd bcd_3 (
    ._3(n3_7seg_decodeer_1_y3), ._2(n3_7seg_decodeer_1_y2), ._1(n3_7seg_decodeer_1_y1),
    .in_4(n3_7seg_decodeer_1_y0), .b(bcd_3_b), .a(bcd_3_a), .g(bcd_3_g), .f(bcd_3_f), .c(bcd_3_c),
    .d(bcd_3_d), .out_11(bcd_3_out_11), .e(bcd_3_e));
  _7_Segment_Display u_7_segment_display_1 (
    .g(bcd_1_g), .f(bcd_1_f), .a(bcd_1_a), .b(bcd_1_b), .e(bcd_1_e), .d(bcd_1_d), .c(bcd_1_c),
    .dp(bcd_1_out_11));
  _7_Segment_Display u_7_segment_display_2 (
    .g(bcd_2_g), .f(bcd_2_f), .a(bcd_2_a), .b(bcd_2_b), .e(bcd_2_e), .d(bcd_2_d), .c(bcd_2_c),
    .dp(bcd_2_out_11));
  _7_Segment_Display u_7_segment_display_3 (
    .g(bcd_3_g), .f(bcd_3_f), .a(bcd_3_a), .b(bcd_3_b), .e(bcd_3_e), .d(bcd_3_d), .c(bcd_3_c),
    .dp(bcd_3_out_11));

  // Notes on the sheet:
  //   Data: pull=down
  //   BUS
  //   RAM
  //   Instruction register
  //   contents of rom_1 (hex, n*v repeats v):
  //   204 204 62*0 4a0 4a0 63*0 240 63*0 8400
  //   Program counter
  //   Instructions
  //   0001
  //   LDA
  //   carry flag
  //   0 flag
endmodule

module bcd (
  input  _3,
  input  _2,
  input  _1,
  input  in_4,
  output b,
  output a,
  output g,
  output f,
  output c,
  output d,
  output out_11,
  output e
);

  wire and_1_out, and_2_out, nor_1_out, nor_2_out, not_1_out, not_2_out, or_1_out, or_2_out, xor_1_out,
       xor_2_out, xor_3_out, xor_4_out;

  xor xor_1 (xor_1_out, _2, _3);
  xor xor_2 (xor_2_out, _2, _1);
  or or_1 (or_1_out, _1, in_4);
  not not_1 (not_1_out, in_4);
  not not_2 (not_2_out, _2);
  nor nor_1 (nor_1_out, _3, or_1_out);
  or or_2 (or_2_out, xor_2_out, not_1_out);
  nor nor_2 (nor_2_out, not_2_out, _1);
  xor xor_3 (xor_3_out, xor_1_out, nor_1_out);
  and and_1 (and_1_out, xor_1_out, or_2_out);
  and and_2 (and_2_out, or_2_out, in_4);
  xor xor_4 (xor_4_out, or_2_out, nor_1_out);
  nor nor_3 (e, nor_2_out, in_4);
  nand nand_1 (b, and_1_out, or_1_out);
  or or_3 (g, xor_4_out, nor_2_out);
  or or_4 (d, and_2_out, e);
  nand nand_2 (f, or_1_out, b);
  or or_5 (a, xor_3_out, d);
  or or_6 (c, f, in_4);

  assign out_11 = _3;
endmodule

module dabble (
  input  i3,
  input  i2,
  input  i1,
  input  i0,
  output o3,
  output o2,
  output o1,
  output o0
);

  wire nor_1_out, nor_2_out, or_1_out, xor_1_out, xor_2_out;

  xor xor_1 (xor_1_out, i0, i3);
  nor nor_1 (nor_1_out, i3, i2);
  xor xor_2 (xor_2_out, i3, i1);
  nor nor_2 (nor_2_out, xor_1_out, xor_2_out);
  nor nor_3 (o3, nor_2_out, nor_1_out);
  or or_1 (or_1_out, xor_1_out, nor_1_out);
  nor nor_4 (o2, or_1_out, i1);
  and and_1 (o1, or_1_out, xor_2_out);
  xor xor_3 (o0, i0, o3);
endmodule

module _3_7seg_decodeer (
  input  in_1,
  input  i7,
  input  in_3,
  input  i6,
  input  i5,
  input  i4,
  input  i3,
  input  i2,
  input  i1,
  input  i0,
  output y9,
  output y8,
  output y7,
  output y6,
  output y5,
  output y4,
  output y3,
  output y2,
  output y1,
  output y0
);

  wire dabble_1_o0, dabble_1_o1, dabble_1_o2, dabble_1_o3, dabble_2_o0, dabble_2_o1, dabble_2_o2,
       dabble_2_o3, dabble_3_o0, dabble_3_o1, dabble_3_o2, dabble_3_o3, dabble_4_o0, dabble_4_o1,
       dabble_4_o2, dabble_4_o3, dabble_5_o0, dabble_5_o1, dabble_5_o2;

  dabble dabble_1 (
    .i3(in_1), .i2(i7), .i1(i6), .i0(i5), .o3(dabble_1_o3), .o2(dabble_1_o2), .o1(dabble_1_o1),
    .o0(dabble_1_o0));
  dabble dabble_2 (
    .i3(dabble_1_o2), .i2(dabble_1_o1), .i1(dabble_1_o0), .i0(i4), .o3(dabble_2_o3), .o2(dabble_2_o2),
    .o1(dabble_2_o1), .o0(dabble_2_o0));
  dabble dabble_3 (
    .i3(dabble_2_o2), .i2(dabble_2_o1), .i1(dabble_2_o0), .i0(i3), .o3(dabble_3_o3), .o2(dabble_3_o2),
    .o1(dabble_3_o1), .o0(dabble_3_o0));
  dabble dabble_4 (
    .i3(dabble_3_o2), .i2(dabble_3_o1), .i1(dabble_3_o0), .i0(i2), .o3(dabble_4_o3), .o2(dabble_4_o2),
    .o1(dabble_4_o1), .o0(dabble_4_o0));
  dabble dabble_5 (
    .i3(in_3), .i2(dabble_1_o3), .i1(dabble_2_o3), .i0(dabble_3_o3), .o3(y9), .o2(dabble_5_o2),
    .o1(dabble_5_o1), .o0(dabble_5_o0));
  dabble dabble_6 (
    .i3(dabble_5_o2), .i2(dabble_5_o1), .i1(dabble_5_o0), .i0(dabble_4_o3), .o3(y8), .o2(y7), .o1(y6), .o0(y5));
  dabble dabble_7 (.i3(dabble_4_o2), .i2(dabble_4_o1), .i1(dabble_4_o0), .i0(i1), .o3(y4), .o2(y3), .o1(y2), .o0(y1));

  assign y0 = i0;
endmodule
