// Logisim project clock.circ as structural Verilog: 1 circuit, main circuit main
module main (
  input  Halt_switch
);

  wire clock_1_out, not_1_out;

  Clock clock_1 (.out(clock_1_out));
  not not_1 (not_1_out, Halt_switch);
  // AND_Gate and_1 has open pins: in0=clock_1_out, in4=not_1_out, out=open
endmodule
