// Logisim project Registers.circ as structural Verilog: 1 circuit, main circuit main
module main (
  input  ain,
  input  aout,
  input  bin,
  input  bout,
  input  in_5,
  input  cin,
  input  cout,
  input  Master_reset,
  input  Halt_switch,
  output [7:0] Bus
);

  wire and_1_out, clock_1_out, not_1_out;
  wire [7:0] bit_extender_1_out, register_1_q, register_2_q, register_3_q;

  Clock clock_1 (.out(clock_1_out));
  not not_1 (not_1_out, Halt_switch);
  and and_1 (and_1_out, clock_1_out, not_1_out);
  Register register_1 (.D(Bus), .en(ain), .Q(register_1_q), .clk(and_1_out), .clr(Master_reset));
  Register register_2 (.D(Bus), .en(bin), .Q(register_2_q), .clk(and_1_out), .clr(Master_reset));
  Register register_3 (.D(Bus), .en(cin), .Q(register_3_q), .clk(and_1_out), .clr(Master_reset));
  assign Bus = aout ? register_1_q : 8'bz;  // Controlled_Buffer controlled_buffer_1
  assign Bus = bout ? register_2_q : 8'bz;  // Controlled_Buffer controlled_buffer_2
  assign bit_extender_1_out = {{4{in_5}}, register_3_q[3:0]};  // Bit_Extender bit_extender_1
  assign Bus = cout ? bit_extender_1_out : 8'bz;  // Controlled_Buffer controlled_buffer_3

  // Notes on the sheet:
  //   Register B
  //   Register C
  //   Instruction Register
  //   Register A
endmodule
