// Logisim project ProgramCounter.circ as structural Verilog: 1 circuit, main circuit main
module main (
  input  switch,
  input  [7:0] manual_address,
  input  ain,
  input  aout,
  input  bin,
  input  bout,
  input  in_7,
  input  [7:0] in_8,
  input  cin,
  input  cout,
  input  Master_reset,
  input  sub,
  input  aluout,
  input  ramout,
  input  ramin,
  input  mai,
  input  jump,
  input  counte,
  input  counto,
  input  Halt_switch,
  output [7:0] Bus
);

  wire and_1_out, clock_1_out, not_1_out, not_2_out;
  wire [7:0] adder_1_out, bit_extender_1_out, bit_extender_2_out, controlled_buffer_4_out,
       controlled_buffer_7_out, counter_1_q, ram_1_data, register_1_q, register_2_q, register_3_q,
       register_4_q, xor_1_out;

  Clock clock_1 (.out(clock_1_out));
  not not_1 (not_1_out, Halt_switch);
  and and_1 (and_1_out, clock_1_out, not_1_out);
  assign bit_extender_1_out = {{7{sub}}, sub};  // Bit_Extender bit_extender_1
  Register register_1 (.D(Bus), .en(ain), .Q(register_1_q), .clk(and_1_out), .clr(Master_reset));
  Register register_2 (.D(Bus), .en(bin), .Q(register_2_q), .clk(and_1_out), .clr(Master_reset));
  Register register_3 (.D(Bus), .en(cin), .Q(register_3_q), .clk(and_1_out), .clr(Master_reset));
  assign xor_1_out = bit_extender_1_out ^ register_2_q;  // XOR_Gate xor_1, 8 bits wide
  assign Bus = aout ? register_1_q : 8'bz;  // Controlled_Buffer controlled_buffer_1
  assign Bus = bout ? register_2_q : 8'bz;  // Controlled_Buffer controlled_buffer_2
  assign bit_extender_2_out = {{4{in_7}}, register_3_q[3:0]};  // Bit_Extender bit_extender_2
  assign Bus = cout ? bit_extender_2_out : 8'bz;  // Controlled_Buffer controlled_buffer_3
  assign controlled_buffer_4_out = not_2_out ? Bus : 8'bz;  // Controlled_Buffer controlled_buffer_4
  assign controlled_buffer_4_out = switch ? in_8 : 8'bz;  // Controlled_Buffer controlled_buffer_5
  Adder adder_1 (.a(register_1_q), .b(xor_1_out), .out(adder_1_out), .cin(sub));  // open: cout
  assign Bus = aluout ? adder_1_out : 8'bz;  // Controlled_Buffer controlled_buffer_6
  Register register_4 (.D(Bus), .en(mai), .Q(register_4_q), .clk(and_1_out), .clr(Master_reset));
  assign controlled_buffer_7_out = not_2_out ? register_4_q : 8'bz;  // Controlled_Buffer controlled_buffer_7
  assign controlled_buffer_7_out = switch ? manual_address : 8'bz;  // Controlled_Buffer controlled_buffer_8
  not not_2 (not_2_out, switch);
  assign Bus = ramout ? ram_1_data : 8'bz;  // Controlled_Buffer controlled_buffer_9
  RAM #(.bus("separate")) ram_1 (
    .addr(controlled_buffer_7_out), .din(controlled_buffer_4_out), .data(ram_1_data), .str(ramin),
    .clk(and_1_out), .ld(ramout), .clr(Master_reset));  // open: sel
  Counter counter_1 (
    .load(jump), .D(Bus), .count(counte), .Q(counter_1_q), .clk(and_1_out), .clr(Master_reset));  // open: carry
  assign Bus = counto ? counter_1_q : 8'bz;  // Controlled_Buffer controlled_buffer_10

  // Notes on the sheet:
  //   Register B
  //   Register C
  //   Instruction Register
  //   xor gate for 2's compliment
  //   Register A
  //   Address Register
  //   data from bus
  //   manual data
  //   Arithmetic
  //   Logic
  //   Unit
  //   programming
  //   Random
  //   Access
  //   Memory
  //   Program Counter
endmodule
