// Logisim project Display.circ as structural Verilog: 1 circuit, main circuit main
module main (
  input  switch,
  input  [7:0] manual_address,
  input  ain,
  input  aout,
  input  bin,
  input  bout,
  input  in_7,
  input  [7:0] in_8,
  input  cin,
  input  cout,
  input  Master_reset,
  input  sub,
  input  aluout,
  input  ramout,
  input  ramin,
  input  mai,
  input  jump,
  input  counte,
  input  counto,
  input  outin,
  input  outo,
  input  Halt_switch,
  output [7:0] Bus
);

  wire and_1_out, clock_1_out, not_1_out, not_2_out;
  wire [7:0] adder_1_out, bit_extender_1_out, bit_extender_2_out, controlled_buffer_4_out,
       controlled_buffer_7_out, controlled_buffer_11_out, counter_1_q, ram_1_data, register_1_q,
       register_2_q, register_3_q, register_4_q, register_5_q, rom_1_data, rom_2_data, rom_3_data, xor_1_out;

  Clock clock_1 (.out(clock_1_out));
  not not_1 (not_1_out, Halt_switch);
  and and_1 (and_1_out, clock_1_out, not_1_out);
  assign bit_extender_1_out = {{7{sub}}, sub};  // Bit_Extender bit_extender_1
  Register register_1 (.D(Bus), .en(ain), .Q(register_1_q), .clk(and_1_out), .clr(Master_reset));
  Register register_2 (.D(Bus), .en(bin), .Q(register_2_q), .clk(and_1_out), .clr(Master_reset));
  Register register_3 (.D(Bus), .en(cin), .Q(register_3_q), .clk(and_1_out), .clr(Master_reset));
  assign xor_1_out = bit_extender_1_out ^ register_2_q;  // XOR_Gate xor_1, 8 bits wide
  assign Bus = aout ? register_1_q : 8'bz;  // Controlled_Buffer controlled_buffer_1
  assign Bus = bout ? register_2_q : 8'bz;  // Controlled_Buffer controlled_buffer_2
  assign bit_extender_2_out = {{4{in_7}}, register_3_q[3:0]};  // Bit_Extender bit_extender_2
  assign Bus = cout ? bit_extender_2_out : 8'bz;  // Controlled_Buffer controlled_buffer_3
  assign controlled_buffer_4_out = not_2_out ? Bus : 8'bz;  // Controlled_Buffer controlled_buffer_4
  assign controlled_buffer_4_out = switch ? in_8 : 8'bz;  // Controlled_Buffer controlled_buffer_5
  Adder adder_1 (.a(register_1_q), .b(xor_1_out), .out(adder_1_out), .cin(sub));  // open: cout
  assign Bus = aluout ? adder_1_out : 8'bz;  // Controlled_Buffer controlled_buffer_6
  Register register_4 (.D(Bus), .en(mai), .Q(register_4_q), .clk(and_1_out), .clr(Master_reset));
  assign controlled_buffer_7_out = not_2_out ? register_4_q : 8'bz;  // Controlled_Buffer controlled_buffer_7
  assign controlled_buffer_7_out = switch ? manual_address : 8'bz;  // Controlled_Buffer controlled_buffer_8
  not not_2 (not_2_out, switch);
  assign Bus = ramout ? ram_1_data : 8'bz;  // Controlled_Buffer controlled_buffer_9
  RAM #(.bus("separate")) ram_1 (
    .addr(controlled_buffer_7_out), .din(controlled_buffer_4_out), .data(ram_1_data), .str(ramin),
    .clk(and_1_out), .ld(ramout), .clr(Master_reset));  // open: sel
  Counter counter_1 (
    .load(jump), .D(Bus), .count(counte), .Q(counter_1_q), .clk(and_1_out), .clr(Master_reset));  // open: carry
  assign Bus = counto ? counter_1_q : 8'bz;  // Controlled_Buffer controlled_buffer_10
  Register register_5 (.D(Bus), .en(outin), .Q(register_5_q), .clk(and_1_out), .clr(Master_reset));
  assign controlled_buffer_11_out = outo ? register_5_q : 8'bz;  // Controlled_Buffer controlled_buffer_11
  _7_Segment_Display u_7_segment_display_1 (
    .g(rom_1_data[3]), .f(rom_1_data[2]), .a(rom_1_data[1]), .b(rom_1_data[0]), .e(rom_1_data[7]),
    .d(rom_1_data[7]), .c(rom_1_data[5]), .dp(rom_1_data[4]));
  ROM rom_1 (.addr(controlled_buffer_11_out), .data({{2{rom_1_data[7]}}, rom_1_data[5:0]}));  // open: sel
  ROM rom_2 (.addr(controlled_buffer_11_out), .data(rom_2_data));  // open: sel
  ROM rom_3 (.addr(controlled_buffer_11_out), .data(rom_3_data));  // open: sel
  _7_Segment_Display u_7_segment_display_2 (
    .g(rom_2_data[3]), .f(rom_2_data[2]), .a(rom_2_data[1]), .b(rom_2_data[0]), .e(rom_2_data[7]),
    .d(rom_2_data[6]), .c(rom_2_data[5]), .dp(rom_2_data[4]));
  _7_Segment_Display u_7_segment_display_3 (
    .g(rom_3_data[3]), .f(rom_3_data[2]), .a(rom_3_data[1]), .b(rom_3_data[0]), .e(rom_3_data[7]),
    .d(rom_3_data[6]), .c(rom_3_data[5]), .dp(rom_3_data[4]));

  // Notes on the sheet:
  //   Register B
  //   Register C
  //   Instruction Register
  //   xor gate for 2's compliment
  //   Register A
  //   Address Register
  //   data from bus
  //   manual data
  //   Arithmetic
  //   Logic
  //   Unit
  //   programming
  //   Random
  //   Access
  //   Memory
  //   Program Counter
  //   Output Register
  //   contents of rom_1 (hex, n*v repeats v):
  //   100*0 100*21 56*cb
  //   contents of rom_2 (hex, n*v repeats v):
  //   10*0 10*21 10*cb 11*6b 10*2d 10*6e 10*ee 10*23 10*ef 10*6f 10*e7 9*21 10*cb 10*6b 10*2d 10*6e 10*ee
  //   10*23 10*ef 10*6f 10*e7 10*21 10*cb 10*6b 10*2d 6*6e
  //   contents of rom_3 (hex, n*v repeats v):
  //   e7 21 cb 6b 2d 6e ee 23 ef 6f e7 21 cb 6b 2d 6e ee 23 ef 6f e7 21 cb 6b 2d 6e ee 23 ef 6f e7 21 cb
  //   6b 2d 6e ee 23 ef 6f e7 21 cb 6b 2d 6e ee 23 ef 6f e7 21 cb 6b 2d 6e ee 23 ef 6f e7 21 cb 6b 2d 6e
  //   ee 23 ef 6f e7 21 cb 6b 2d 6e ee 23 ef 6f e7 21 cb 6b 2d 6e ee 23 ef 6f e7 21 cb 6b 2d 6e ee 23 ef
  //   6f e7 21 cb 6b 2d 6e ee 23 ef 6f e7 21 cb 6b 2d 6e ee 23 ef 6f e7 21 cb 6b 2d 6e ee 23 ef 6f e7 21
  //   cb 6b 2d 6e ee 23 ef 6f e7 21 cb 6b 2d 6e ee 23 ef 6f e7 21 cb 6b 2d 6e ee 23 ef 6f e7 21 cb 6b 2d
  //   6e ee 23 ef 6f e7 21 cb 6b 2d 6e ee 23 ef 6f e7 21 cb 6b 2d 6e ee 23 ef 6f e7 21 cb 6b 2d 6e ee 23
  //   ef 6f e7 21 cb 6b 2d 6e ee 23 ef 6f e7 21 cb 6b 2d 6e ee 23 ef 6f e7 21 cb 6b 2d 6e ee 23 ef 6f e7
  //   21 cb 6b 2d 6e ee 23 ef 6f e7 21 cb 6b 2d 6e ee 23 ef 6f e7 21 cb 6b 2d 6e
  //   ROM programmed to decode 7 segment display
endmodule
