// Logisim project Flag.circ as structural Verilog: 1 circuit, main circuit main
module main (
  input  switch,
  input  [7:0] manual_address,
  input  in_3,
  input  [7:0] in_4,
  input  Master_reset,
  output [7:0] Bus,
  output ain,
  output aout,
  output bin,
  output bout,
  output cin,
  output cout,
  output mireset,
  output sub,
  output aluout,
  output ramout,
  output ramin,
  output mai,
  output jump,
  output counte,
  output counto,
  output outin,
  output flagi,
  output Halt_switch
);

  wire and_1_out, clock_1_out, not_1_out, not_2_out;
  wire [1:0] adder_1_cout;
  wire [3:0] register_3_q;
  wire [7:0] adder_1_out, bit_extender_1_out, bit_extender_2_out, controlled_buffer_4_out,
       controlled_buffer_7_out, counter_2_q, not_3_out, ram_1_data, register_1_q, register_2_q, register_4_q,
       register_6_q, rom_2_data, rom_3_data, rom_4_data, xor_1_out;
  wire [9:0] counter_1_q;

  Clock clock_1 (.out(clock_1_out));
  not not_1 (not_1_out, Halt_switch);
  and and_1 (and_1_out, clock_1_out, not_1_out);
  assign bit_extender_1_out = {{7{sub}}, sub};  // Bit_Extender bit_extender_1
  Register register_1 (.D(Bus), .en(ain), .Q(register_1_q), .clk(and_1_out), .clr(Master_reset));
  Register register_2 (.D(Bus), .en(bin), .Q(register_2_q), .clk(and_1_out), .clr(Master_reset));
  Register register_3 (.D(Bus), .en(cin), .Q({counter_1_q[7:4], register_3_q}), .clk(and_1_out), .clr(Master_reset));
  assign xor_1_out = bit_extender_1_out ^ register_2_q;  // XOR_Gate xor_1, 8 bits wide
  assign Bus = aout ? register_1_q : 8'bz;  // Controlled_Buffer controlled_buffer_1
  assign Bus = bout ? register_2_q : 8'bz;  // Controlled_Buffer controlled_buffer_2
  assign bit_extender_2_out = {{4{in_3}}, register_3_q};  // Bit_Extender bit_extender_2
  Counter #(.width(4), .max('hf)) counter_1 (
    .Q(counter_1_q[3:0]), .clk(and_1_out), .clr(mireset));  // open: load, D, count, carry
  assign Bus = cout ? bit_extender_2_out : 8'bz;  // Controlled_Buffer controlled_buffer_3
  assign controlled_buffer_4_out = not_2_out ? Bus : 8'bz;  // Controlled_Buffer controlled_buffer_4
  assign controlled_buffer_4_out = switch ? in_4 : 8'bz;  // Controlled_Buffer controlled_buffer_5
  Adder adder_1 (.a(register_1_q), .b(xor_1_out), .out(adder_1_out), .cin(sub), .cout(adder_1_cout[0]));
  assign Bus = aluout ? adder_1_out : 8'bz;  // Controlled_Buffer controlled_buffer_6
  ROM #(.addrWidth(10), .dataWidth(18)) rom_1 (
    .addr(counter_1_q),
    .data({ain, aout, bin, bout, cin, cout, mireset, sub, aluout, ramout, ramin, mai, jump, counte, counto, outin, flagi, Halt_switch}));  // open: sel
  Register register_4 (.D(Bus), .en(mai), .Q(register_4_q), .clk(and_1_out), .clr(Master_reset));
  assign controlled_buffer_7_out = not_2_out ? register_4_q : 8'bz;  // Controlled_Buffer controlled_buffer_7
  assign controlled_buffer_7_out = switch ? manual_address : 8'bz;  // Controlled_Buffer controlled_buffer_8
  not not_2 (not_2_out, switch);
  assign Bus = ramout ? ram_1_data : 8'bz;  // Controlled_Buffer controlled_buffer_9
  RAM #(.bus("separate")) ram_1 (
    .addr(controlled_buffer_7_out), .din(controlled_buffer_4_out), .data(ram_1_data), .str(ramin),
    .clk(and_1_out), .ld(ramout), .clr(Master_reset));  // open: sel
  Counter counter_2 (
    .load(jump), .D(Bus), .count(counte), .Q(counter_2_q), .clk(and_1_out), .clr(Master_reset));  // open: carry
  assign Bus = counto ? counter_2_q : 8'bz;  // Controlled_Buffer controlled_buffer_10
  Register #(.width(2)) register_5 (
    .D(adder_1_cout), .en(flagi), .Q(counter_1_q[9:8]), .clk(and_1_out), .clr(Master_reset));
  assign not_3_out = ~adder_1_out;  // NOT_Gate not_3, 8 bits wide
  Register register_6 (.D(Bus), .en(outin), .Q(register_6_q), .clk(and_1_out), .clr(Master_reset));
  and and_2 (adder_1_cout[1], not_3_out[0], not_3_out[1], not_3_out[2], not_3_out[3], not_3_out[4], not_3_out[5], not_3_out[6], not_3_out[7]);
  _7_Segment_Display u_7_segment_display_1 (
    .g(rom_2_data[3]), .f(rom_2_data[2]), .a(rom_2_data[1]), .b(rom_2_data[0]), .e(rom_2_data[7]),
    .d(rom_2_data[7]), .c(rom_2_data[5]), .dp(rom_2_data[4]));
  ROM rom_2 (.addr(register_6_q), .data({{2{rom_2_data[7]}}, rom_2_data[5:0]}));  // open: sel
  ROM rom_3 (.addr(register_6_q), .data(rom_3_data));  // open: sel
  ROM rom_4 (.addr(register_6_q), .data(rom_4_data));  // open: sel
  _7_Segment_Display u_7_segment_display_2 (
    .g(rom_3_data[3]), .f(rom_3_data[2]), .a(rom_3_data[1]), .b(rom_3_data[0]), .e(rom_3_data[7]),
    .d(rom_3_data[6]), .c(rom_3_data[5]), .dp(rom_3_data[4]));
  _7_Segment_Display u_7_segment_display_3 (
    .g(rom_4_data[3]), .f(rom_4_data[2]), .a(rom_4_data[1]), .b(rom_4_data[0]), .e(rom_4_data[7]),
    .d(rom_4_data[6]), .c(rom_4_data[5]), .dp(rom_4_data[4]));

  // Notes on the sheet:
  //   Register B
  //   Register C
  //   Instruction Register
  //   xor gate for 2's compliment
  //   Register A
  //   Micro-Instruction Counter
  //   Address Register
  //   data from bus
  //   manual data
  //   Arithmetic
  //   Logic
  //   Unit
  //   Control logic
  //   contents of rom_1 (hex, n*v repeats v):
  //   48 2110 800 13*0 48 2110 1040 20100 800 11*0 48 2110 1040 8100 20200 800 10*0 48 2110 10004 800 12*0
  //   48 2110 1020 800
  //   programming
  //   Random
  //   Access
  //   Memory
  //   Program Counter
  //   Output Register
  //   8 bit instruction
  //   ADD  0010
  //   OUT 0011
  //   2 bit Flag Register
  //   Some pre-coded Instruction: 
  //   LDA 0001 [Memory Address]
  //   [Memory Address]
  //   JMP  0100  [Instruction Address]
  //   carry and zero flag
  //   contents of rom_2 (hex, n*v repeats v):
  //   100*0 100*21 56*cb
  //   contents of rom_3 (hex, n*v repeats v):
  //   10*0 10*21 10*cb 11*6b 10*2d 10*6e 10*ee 10*23 10*ef 10*6f 10*e7 9*21 10*cb 10*6b 10*2d 10*6e 10*ee
  //   10*23 10*ef 10*6f 10*e7 10*21 10*cb 10*6b 10*2d 6*6e
  //   contents of rom_4 (hex, n*v repeats v):
  //   e7 21 cb 6b 2d 6e ee 23 ef 6f e7 21 cb 6b 2d 6e ee 23 ef 6f e7 21 cb 6b 2d 6e ee 23 ef 6f e7 21 cb
  //   6b 2d 6e ee 23 ef 6f e7 21 cb 6b 2d 6e ee 23 ef 6f e7 21 cb 6b 2d 6e ee 23 ef 6f e7 21 cb 6b 2d 6e
  //   ee 23 ef 6f e7 21 cb 6b 2d 6e ee 23 ef 6f e7 21 cb 6b 2d 6e ee 23 ef 6f e7 21 cb 6b 2d 6e ee 23 ef
  //   6f e7 21 cb 6b 2d 6e ee 23 ef 6f e7 21 cb 6b 2d 6e ee 23 ef 6f e7 21 cb 6b 2d 6e ee 23 ef 6f e7 21
  //   cb 6b 2d 6e ee 23 ef 6f e7 21 cb 6b 2d 6e ee 23 ef 6f e7 21 cb 6b 2d 6e ee 23 ef 6f e7 21 cb 6b 2d
  //   6e ee 23 ef 6f e7 21 cb 6b 2d 6e ee 23 ef 6f e7 21 cb 6b 2d 6e ee 23 ef 6f e7 21 cb 6b 2d 6e ee 23
  //   ef 6f e7 21 cb 6b 2d 6e ee 23 ef 6f e7 21 cb 6b 2d 6e ee 23 ef 6f e7 21 cb 6b 2d 6e ee 23 ef 6f e7
  //   21 cb 6b 2d 6e ee 23 ef 6f e7 21 cb 6b 2d 6e ee 23 ef 6f e7 21 cb 6b 2d 6e
  //   ROM programmed to decode 7 segment display
  //   (display data from register A)
  //   (loads data  from memory address to register A]
  //   (adds data from memory address to register A and stores in register A)
  //   {jump to the memory address of the instruction)
endmodule
